// Logisim project 8-bit-full-processor.circ as structural Verilog: 22 circuits, main circuit main
module main (
  input  [7:0] in_1,
  input  EN,
  input  [2:0] OP_CODE,
  output [3:0] PC_CONTENTT,
  output [3:0] MAR_CON,
  output [7:0] MBR_CON,
  output [7:0] IR_CONTENTT,
  output [2:0] COUNTER_CON,
  output [7:0] R1_CONTENTT,
  output [7:0] ACC_CON,
  output [7:0] ALU_CONTENTT,
  output [7:0] R2_CONTENT
);

  wire clock_1_out, cu_1_c0, cu_1_c1, cu_1_c2, cu_1_c3, cu_1_c4, cu_1_c5, cu_1_c6, cu_1_c7, cu_1_c8, cu_1_c9,
       cu_1_c10, cu_1_c11, cu_2_1_c12, cu_2_1_c13, cu_2_1_c14, cu_2_1_c15, cu_2_1_c16, cu_2_1_c17;
  wire [3:0] bitselector_2_out, controlled_buffer_1_out, mar_1_do;
  wire [7:0] ir_1_do, R1_content, R2_content_2;

  Clock clock_1 (.out(clock_1_out));
  PC pc_1 (
    .D(controlled_buffer_1_out), .JMP(cu_1_c1), .CLK(clock_1_out), .OE(cu_1_c0), .OUTPUT(PC_CONTENTT));  // open: RESET
  IR ir_1 (
    .DI(ALU_CONTENTT), .load(cu_1_c7), .CLK(clock_1_out), .OE(cu_1_c8), .CONTENT(IR_CONTENTT), .DO(ir_1_do));  // open: RESET
  REGISTER R1 (
    .in_1(ALU_CONTENTT), .load(cu_2_1_c12), .CLK(clock_1_out), .OE(1'b1), .CONTENT(R1_content),
    .DO(R1_CONTENTT));  // open: RESET
  ALU alu_1 (.D_I1(R1_content), .D_I2(R2_content_2), .EN(cu_1_c11), .OP_code(ir_1_do[2:0]), .out_5(ALU_CONTENTT));
  REGISTER R2 (
    .in_1(ALU_CONTENTT), .load(cu_2_1_c13), .CLK(clock_1_out), .OE(1'b1), .CONTENT(R2_content_2),
    .DO(R2_CONTENT));  // open: RESET
  assign controlled_buffer_1_out = cu_1_c0 ? PC_CONTENTT : 4'bz;  // Controlled_Buffer controlled_buffer_1
  BitSelector #(.group(4)) bitselector_1 (.in(ir_1_do), .out(controlled_buffer_1_out), .sel(cu_1_c8));
  assign ALU_CONTENTT = EN ? in_1 : 8'bz;  // Controlled_Buffer controlled_buffer_2
  MAR mar_1 (
    .DI(controlled_buffer_1_out), .load(cu_1_c9), .CLK(clock_1_out), .RESET(cu_2_1_c16), .OE(cu_1_c10),
    .CONTENT(MAR_CON), .DO(mar_1_do));
  assign ALU_CONTENTT = cu_1_c5 ? ALU_CONTENTT : 8'bz;  // Controlled_Buffer controlled_buffer_3
  REGISTER register_1 (
    .in_1(ALU_CONTENTT), .load(cu_2_1_c15), .CLK(clock_1_out), .OE(cu_2_1_c14), .CONTENT(ACC_CON),
    .DO(ALU_CONTENTT));  // open: RESET
  MBR mbr_1 (
    .DI(ALU_CONTENTT), .load(cu_1_c4), .CLK(clock_1_out), .OE(cu_1_c6), .CONTENT(MBR_CON), .DO(ALU_CONTENTT));  // open: RESET
  RAM #(.addrWidth(4), .bus("separate")) ram_1 (
    .addr(mar_1_do), .din(ALU_CONTENTT), .data(ALU_CONTENTT), .str(cu_1_c2), .clk(clock_1_out), .ld(cu_1_c3));  // open: sel, clr
  BitSelector #(.group(4)) bitselector_2 (.in(IR_CONTENTT), .out(bitselector_2_out), .sel(1'b1));
  Counter #(.width(3), .max('h7)) step_counter (
    .Q(COUNTER_CON), .clk(clock_1_out), .clr(cu_2_1_c17));  // open: load, D, count, carry
  CU cu_1 (
    .OPC3(bitselector_2_out[3]), .OPC2(bitselector_2_out[2]), .OPC1(bitselector_2_out[1]),
    .OPC0(bitselector_2_out[0]), .SC2(COUNTER_CON[2]), .SC1(COUNTER_CON[1]), .SC0(COUNTER_CON[0]),
    .C0(cu_1_c0), .C1(cu_1_c1), .C2(cu_1_c2), .C3(cu_1_c3), .C4(cu_1_c4), .C5(cu_1_c5), .C6(cu_1_c6),
    .C7(cu_1_c7), .C8(cu_1_c8), .C9(cu_1_c9), .C10(cu_1_c10), .C11(cu_1_c11));
  CU_2 cu_2_1 (
    .OPC3(bitselector_2_out[3]), .OPC2(bitselector_2_out[2]), .OPC1(bitselector_2_out[1]),
    .OPC0(bitselector_2_out[0]), .SC2(COUNTER_CON[2]), .SC1(COUNTER_CON[1]), .SC0(COUNTER_CON[0]),
    .C12(cu_2_1_c12), .C13(cu_2_1_c13), .C14(cu_2_1_c14), .C15(cu_2_1_c15), .C16(cu_2_1_c16), .C17(cu_2_1_c17));

  // Notes on the sheet:
  //   INTERNAL ADDRESS BUS
  //   INTERNAL DATA BUS
  //   EXTERNAL DATA BUS
  //   EXTERNAL DATA BUS
  //   C15
  //   C14
  //   C13
  //   C12
  //   C11
  //   C10
  //   C9
  //   C8
  //   C7
  //   C6
  //   C5
  //   C4
  //   C3
  //   C2
  //   C1
  //   C0
  //   C0
  //   C1
  //   C2
  //   C3
  //   C4
  //   C5
  //   C6
  //   C7
  //   C8
  //   C9
  //   C10
  //   C11
  //   C12
  //   C13
  //   C14
  //   C15
  //   ALU OP CODE
  //   000 
  //   001 
  //   010
  //   011
  //   100
  //   101
  //   110
  //   111
  //   CU CONTENT
  //   PC OE
  //   PC INC
  //   RAM WE
  //   RAM OE
  //   MBR WE
  //   MBR BUS EN
  //   MBR OE
  //   IR WE
  //   IR OE
  //   MAR WE
  //   MAR OE
  //   ALU OE
  //   REG_1 WE
  //   REG_2 WE
  //   ACC OE
  //   ACC WE
  //   ADD
  //   SUB
  //   MUL
  //   DIV
  //   NAND
  //   NOR
  //   XOR
  //   XNOR
endmodule

module REGISTER (
  input  [7:0] in_1,
  input  load,
  input  CLK,
  input  RESET,
  input  OE,
  output [7:0] CONTENT,
  output [7:0] DO
);

  wire and_1_out, and_2_out, and_3_out, and_4_out, and_5_out, and_6_out, and_7_out, and_8_out, and_9_out,
       and_10_out, and_11_out, and_12_out, and_13_out, and_14_out, and_15_out, and_16_out, not_1_out,
       or_1_out, or_2_out, or_3_out, or_4_out, or_5_out, or_6_out, or_7_out, or_8_out;

  not not_1 (not_1_out, load);
  and and_1 (and_1_out, in_1[7], load);
  or or_1 (or_1_out, and_1_out, and_2_out);
  and and_2 (and_2_out, not_1_out, CONTENT[7]);
  and and_3 (and_3_out, in_1[6], load);
  D_Flip_Flop d_ff_1 (.clk(CLK), .D(or_1_out), .Q(CONTENT[7]), .reset(RESET));  // open: Qn, preset, en
  and and_4 (and_4_out, not_1_out, CONTENT[6]);
  or or_2 (or_2_out, and_3_out, and_4_out);
  and and_5 (and_5_out, in_1[5], load);
  or or_3 (or_3_out, and_5_out, and_6_out);
  D_Flip_Flop d_ff_2 (.clk(CLK), .D(or_2_out), .Q(CONTENT[6]), .reset(RESET));  // open: Qn, preset, en
  and and_6 (and_6_out, not_1_out, CONTENT[5]);
  D_Flip_Flop d_ff_3 (.clk(CLK), .D(or_3_out), .Q(CONTENT[5]), .reset(RESET));  // open: Qn, preset, en
  and and_7 (and_7_out, in_1[4], load);
  or or_4 (or_4_out, and_7_out, and_8_out);
  and and_8 (and_8_out, not_1_out, CONTENT[4]);
  D_Flip_Flop d_ff_4 (.clk(CLK), .D(or_4_out), .Q(CONTENT[4]), .reset(RESET));  // open: Qn, preset, en
  and and_9 (and_9_out, in_1[3], load);
  and and_10 (and_10_out, not_1_out, CONTENT[3]);
  or or_5 (or_5_out, and_9_out, and_10_out);
  D_Flip_Flop d_ff_5 (.clk(CLK), .D(or_5_out), .Q(CONTENT[3]), .reset(RESET));  // open: Qn, preset, en
  and and_11 (and_11_out, in_1[2], load);
  or or_6 (or_6_out, and_11_out, and_13_out);
  and and_12 (and_12_out, in_1[1], load);
  and and_13 (and_13_out, not_1_out, CONTENT[2]);
  D_Flip_Flop d_ff_6 (.clk(CLK), .D(or_6_out), .Q(CONTENT[2]), .reset(RESET));  // open: Qn, preset, en
  and and_14 (and_14_out, not_1_out, CONTENT[1]);
  or or_7 (or_7_out, and_12_out, and_14_out);
  D_Flip_Flop d_ff_7 (.clk(CLK), .D(or_7_out), .Q(CONTENT[1]), .reset(RESET));  // open: Qn, preset, en
  and and_15 (and_15_out, in_1[0], load);
  or or_8 (or_8_out, and_15_out, and_16_out);
  and and_16 (and_16_out, not_1_out, CONTENT[0]);
  D_Flip_Flop d_ff_8 (.clk(CLK), .D(or_8_out), .Q(CONTENT[0]), .reset(RESET));  // open: Qn, preset, en
  assign DO = OE ? CONTENT : 8'bz;  // Controlled_Buffer controlled_buffer_1
endmodule

module MBR (
  input  [7:0] DI,
  input  load,
  input  CLK,
  input  RESET,
  input  OE,
  output [7:0] CONTENT,
  output [7:0] DO
);

  wire and_1_out, and_2_out, and_3_out, and_4_out, and_5_out, and_6_out, and_7_out, and_8_out, and_9_out,
       and_10_out, and_11_out, and_12_out, and_13_out, and_14_out, and_15_out, and_16_out, not_1_out,
       or_1_out, or_2_out, or_3_out, or_4_out, or_5_out, or_6_out, or_7_out, or_8_out;

  not not_1 (not_1_out, load);
  and and_1 (and_1_out, DI[7], load);
  or or_1 (or_1_out, and_1_out, and_3_out);
  and and_2 (and_2_out, DI[6], load);
  and and_3 (and_3_out, not_1_out, CONTENT[7]);
  D_Flip_Flop d_ff_1 (.clk(CLK), .D(or_1_out), .Q(CONTENT[7]), .reset(RESET));  // open: Qn, preset, en
  and and_4 (and_4_out, not_1_out, CONTENT[6]);
  or or_2 (or_2_out, and_2_out, and_4_out);
  and and_5 (and_5_out, DI[5], load);
  or or_3 (or_3_out, and_5_out, and_6_out);
  D_Flip_Flop d_ff_2 (.clk(CLK), .D(or_2_out), .Q(CONTENT[6]), .reset(RESET));  // open: Qn, preset, en
  and and_6 (and_6_out, not_1_out, CONTENT[5]);
  D_Flip_Flop d_ff_3 (.clk(CLK), .D(or_3_out), .Q(CONTENT[5]), .reset(RESET));  // open: Qn, preset, en
  and and_7 (and_7_out, DI[4], load);
  or or_4 (or_4_out, and_7_out, and_8_out);
  and and_8 (and_8_out, not_1_out, CONTENT[4]);
  D_Flip_Flop d_ff_4 (.clk(CLK), .D(or_4_out), .Q(CONTENT[4]), .reset(RESET));  // open: Qn, preset, en
  and and_9 (and_9_out, DI[3], load);
  and and_10 (and_10_out, not_1_out, CONTENT[3]);
  or or_5 (or_5_out, and_9_out, and_10_out);
  D_Flip_Flop d_ff_5 (.clk(CLK), .D(or_5_out), .Q(CONTENT[3]), .reset(RESET));  // open: Qn, preset, en
  and and_11 (and_11_out, DI[2], load);
  or or_6 (or_6_out, and_11_out, and_13_out);
  and and_12 (and_12_out, DI[1], load);
  and and_13 (and_13_out, not_1_out, CONTENT[2]);
  D_Flip_Flop d_ff_6 (.clk(CLK), .D(or_6_out), .Q(CONTENT[2]), .reset(RESET));  // open: Qn, preset, en
  and and_14 (and_14_out, not_1_out, CONTENT[1]);
  or or_7 (or_7_out, and_12_out, and_14_out);
  D_Flip_Flop d_ff_7 (.clk(CLK), .D(or_7_out), .Q(CONTENT[1]), .reset(RESET));  // open: Qn, preset, en
  and and_15 (and_15_out, DI[0], load);
  or or_8 (or_8_out, and_15_out, and_16_out);
  and and_16 (and_16_out, not_1_out, CONTENT[0]);
  D_Flip_Flop d_ff_8 (.clk(CLK), .D(or_8_out), .Q(CONTENT[0]), .reset(RESET));  // open: Qn, preset, en
  assign DO = OE ? CONTENT : 8'bz;  // Controlled_Buffer controlled_buffer_1
endmodule

module MAR (
  input  [3:0] DI,
  input  load,
  input  CLK,
  input  RESET,
  input  OE,
  output [3:0] CONTENT,
  output [3:0] DO
);

  wire and_1_out, and_2_out, and_3_out, and_4_out, and_5_out, and_6_out, and_7_out, and_8_out, not_1_out,
       or_1_out, or_2_out, or_3_out, or_4_out;

  not not_1 (not_1_out, load);
  and and_1 (and_1_out, DI[3], load);
  or or_1 (or_1_out, and_1_out, and_3_out);
  and and_2 (and_2_out, DI[2], load);
  and and_3 (and_3_out, not_1_out, CONTENT[3]);
  D_Flip_Flop d_ff_1 (.clk(CLK), .D(or_1_out), .Q(CONTENT[3]), .reset(RESET));  // open: Qn, preset, en
  and and_4 (and_4_out, not_1_out, CONTENT[2]);
  or or_2 (or_2_out, and_2_out, and_4_out);
  and and_5 (and_5_out, DI[1], load);
  or or_3 (or_3_out, and_5_out, and_6_out);
  D_Flip_Flop d_ff_2 (.clk(CLK), .D(or_2_out), .Q(CONTENT[2]), .reset(RESET));  // open: Qn, preset, en
  and and_6 (and_6_out, not_1_out, CONTENT[1]);
  D_Flip_Flop d_ff_3 (.clk(CLK), .D(or_3_out), .Q(CONTENT[1]), .reset(RESET));  // open: Qn, preset, en
  and and_7 (and_7_out, DI[0], load);
  or or_4 (or_4_out, and_7_out, and_8_out);
  and and_8 (and_8_out, not_1_out, CONTENT[0]);
  D_Flip_Flop d_ff_4 (.clk(CLK), .D(or_4_out), .Q(CONTENT[0]), .reset(RESET));  // open: Qn, preset, en
  assign DO = OE ? CONTENT : 4'bz;  // Controlled_Buffer controlled_buffer_1
endmodule

module PC (
  input  [3:0] D,
  input  JMP,
  input  CLK,
  input  RESET,
  input  OE,
  output [3:0] OUTPUT
);

  wire [3:0] adder_1_out, multiplexer_1_out;

  Multiplexer #(.width(4), .enable("false")) multiplexer_1 (
    .in0(D), .in1(adder_1_out), .out(multiplexer_1_out), .sel(JMP));
  MAR mar_1 (.DI(multiplexer_1_out), .load(1'b1), .CLK(CLK), .RESET(RESET), .OE(OE), .CONTENT(OUTPUT));  // open: DO
  Adder #(.width(4)) adder_1 (.a(OUTPUT), .b(4'b0001), .out(adder_1_out));  // open: cin, cout
endmodule

module ACC (
  input  [7:0] DI,
  input  load,
  input  CLK,
  input  RESET,
  input  OE,
  output [7:0] CONTENT,
  output [7:0] DO
);

  wire and_1_out, and_2_out, and_3_out, and_4_out, and_5_out, and_6_out, and_7_out, and_8_out, and_9_out,
       and_10_out, and_11_out, and_12_out, and_13_out, and_14_out, and_15_out, and_16_out, not_1_out,
       or_1_out, or_2_out, or_3_out, or_4_out, or_5_out, or_6_out, or_7_out, or_8_out;

  not not_1 (not_1_out, load);
  and and_1 (and_1_out, DI[7], load);
  or or_1 (or_1_out, and_1_out, and_2_out);
  and and_2 (and_2_out, not_1_out, CONTENT[7]);
  and and_3 (and_3_out, DI[6], load);
  D_Flip_Flop d_ff_1 (.clk(CLK), .D(or_1_out), .Q(CONTENT[7]), .reset(RESET));  // open: Qn, preset, en
  and and_4 (and_4_out, not_1_out, CONTENT[6]);
  or or_2 (or_2_out, and_3_out, and_4_out);
  and and_5 (and_5_out, DI[5], load);
  or or_3 (or_3_out, and_5_out, and_6_out);
  D_Flip_Flop d_ff_2 (.clk(CLK), .D(or_2_out), .Q(CONTENT[6]), .reset(RESET));  // open: Qn, preset, en
  and and_6 (and_6_out, not_1_out, CONTENT[5]);
  D_Flip_Flop d_ff_3 (.clk(CLK), .D(or_3_out), .Q(CONTENT[5]), .reset(RESET));  // open: Qn, preset, en
  and and_7 (and_7_out, DI[4], load);
  or or_4 (or_4_out, and_7_out, and_8_out);
  and and_8 (and_8_out, not_1_out, CONTENT[4]);
  D_Flip_Flop d_ff_4 (.clk(CLK), .D(or_4_out), .Q(CONTENT[4]), .reset(RESET));  // open: Qn, preset, en
  and and_9 (and_9_out, DI[3], load);
  and and_10 (and_10_out, not_1_out, CONTENT[3]);
  or or_5 (or_5_out, and_9_out, and_10_out);
  D_Flip_Flop d_ff_5 (.clk(CLK), .D(or_5_out), .Q(CONTENT[3]), .reset(RESET));  // open: Qn, preset, en
  and and_11 (and_11_out, DI[2], load);
  or or_6 (or_6_out, and_11_out, and_12_out);
  and and_12 (and_12_out, not_1_out, CONTENT[2]);
  and and_13 (and_13_out, DI[1], load);
  D_Flip_Flop d_ff_6 (.clk(CLK), .D(or_6_out), .Q(CONTENT[2]), .reset(RESET));  // open: Qn, preset, en
  and and_14 (and_14_out, not_1_out, CONTENT[1]);
  or or_7 (or_7_out, and_13_out, and_14_out);
  D_Flip_Flop d_ff_7 (.clk(CLK), .D(or_7_out), .Q(CONTENT[1]), .reset(RESET));  // open: Qn, preset, en
  and and_15 (and_15_out, DI[0], load);
  or or_8 (or_8_out, and_15_out, and_16_out);
  and and_16 (and_16_out, not_1_out, CONTENT[0]);
  D_Flip_Flop d_ff_8 (.clk(CLK), .D(or_8_out), .Q(CONTENT[0]), .reset(RESET));  // open: Qn, preset, en
  assign DO = OE ? CONTENT : 8'bz;  // Controlled_Buffer controlled_buffer_1
endmodule

module ALU (
  input  [7:0] D_I1,
  input  [7:0] D_I2,
  input  EN,
  input  [2:0] OP_code,
  output [7:0] out_5
);

  wire and_1_out, and_2_out, and_3_out, and_4_out, and_5_out, and_6_out, and_7_out, and_8_out, not_1_out,
       not_2_out, not_3_out;
  wire [7:0] divider_1_out_4, full_adder_1_sout, multiplier_1_out_4, nand_1_out_4, nor_1_out_4,
       subtracter_1_out, xnor_1_out_4, xor_1_out_4;

  not not_1 (not_1_out, OP_code[2]);
  not not_2 (not_2_out, OP_code[1]);
  not not_3 (not_3_out, OP_code[0]);
  and and_1 (and_1_out, not_1_out, EN, not_2_out, not_3_out);
  and and_2 (and_2_out, not_1_out, EN, not_2_out, OP_code[0]);
  and and_3 (and_3_out, not_1_out, EN, OP_code[1], not_3_out);
  and and_4 (and_4_out, not_1_out, EN, OP_code[1], OP_code[0]);
  and and_5 (and_5_out, OP_code[2], EN, not_2_out, not_3_out);
  and and_6 (and_6_out, OP_code[2], EN, not_2_out, OP_code[0]);
  and and_7 (and_7_out, OP_code[2], EN, OP_code[1], not_3_out);
  and and_8 (and_8_out, OP_code[2], EN, OP_code[1], OP_code[0]);
  FULL_ADDER full_adder_1 (.D_I1(D_I1), .D_I2(D_I2), .EN(and_1_out), .Sout(full_adder_1_sout));  // open: Co
  SUBTRACTER subtracter_1 (.d1(D_I1), .d2(D_I2), .EN(and_2_out), .out(subtracter_1_out));  // open: d
  MULTIPLIER multiplier_1 (.in_1(D_I1), .in_2(D_I2), .in_3(and_3_out), .out_4(multiplier_1_out_4));
  DIVIDER divider_1 (.in_1(D_I1), .in_2(D_I2), .in_3(and_4_out), .out_4(divider_1_out_4));
  NAND nand_1 (.EN(and_5_out), .in_2(D_I1), .in_3(D_I2), .out_4(nand_1_out_4));
  NOR nor_1 (.EN(and_6_out), .in_2(D_I1), .in_3(D_I2), .out_4(nor_1_out_4));
  \xor  xor_1 (.EN(and_7_out), .in_2(D_I1), .in_3(D_I2), .out_4(xor_1_out_4));
  XNOR xnor_1 (.EN(and_8_out), .in_2(D_I1), .in_3(D_I2), .out_4(xnor_1_out_4));
  Multiplexer #(.select(3), .width(8)) multiplexer_1 (
    .in0(full_adder_1_sout), .in1(subtracter_1_out), .in2(multiplier_1_out_4), .in3(divider_1_out_4),
    .in4(nand_1_out_4), .in5(nor_1_out_4), .in6(xor_1_out_4), .in7(xnor_1_out_4), .out(out_5), .sel(OP_code),
    .en(EN));
endmodule

// 1BIT
module ADDDER_UNIT (
  input  in_1,
  input  in_2,
  input  in_3,
  input  in_4,
  output out_5,
  output out_6
);

  wire and_1_out, and_2_out, xor_unit_1_out_4;

  XOR_unit xor_unit_1 (.en(in_1), .in_2(in_2), .in_3(in_3), .out_4(xor_unit_1_out_4));
  XOR_unit xor_unit_2 (.en(in_1), .in_2(xor_unit_1_out_4), .in_3(in_4), .out_4(out_5));
  and and_1 (and_1_out, in_4, in_1, xor_unit_1_out_4);
  and and_2 (and_2_out, in_3, in_1, in_2);
  or or_1 (out_6, and_1_out, and_2_out);
endmodule

// SUB
module SUBTRACTER (
  input  [7:0] d1,
  input  [7:0] d2,
  input  EN,
  output [7:0] out,
  output d
);

  wire [7:0] n2nd_complement_1_out_3;

  _2ND_COMPLEMENT u_2nd_complement_1 (.DI(d2), .EN(EN), .out_3(n2nd_complement_1_out_3));
  FULL_ADDER full_adder_1 (.D_I1(d1), .D_I2(n2nd_complement_1_out_3), .EN(EN), .Sout(out), .Co(d));
endmodule

// MULT
module MULTIPLIER (
  input  [7:0] in_1,
  input  [7:0] in_2,
  input  in_3,
  output [7:0] out_4
);

  wire [7:0] multiplier_1_out;

  Multiplier multiplier_1 (.a(in_1), .b(in_2), .out(multiplier_1_out));  // open: cin, cout
  Multiplexer #(.width(8)) multiplexer_1 (.in0(multiplier_1_out), .out(out_4), .sel(1'b0), .en(in_3));  // open: in1
endmodule

// DIV
module DIVIDER (
  input  [7:0] in_1,
  input  [7:0] in_2,
  input  in_3,
  output [7:0] out_4
);

  wire [7:0] divider_1_out;

  Divider divider_1 (.a(in_1), .b(in_2), .out(divider_1_out));  // open: upper, rem
  Multiplexer #(.width(8)) multiplexer_1 (.in0(divider_1_out), .out(out_4), .sel(1'b0), .en(in_3));  // open: in1
endmodule

module XOR_unit (
  input  en,
  input  in_2,
  input  in_3,
  output out_4
);

  wire and_1_out, and_2_out, not_1_out, not_2_out;

  not not_1 (not_1_out, in_3);
  not not_2 (not_2_out, in_2);
  and and_1 (and_1_out, in_2, en, not_1_out);
  and and_2 (and_2_out, not_2_out, en, in_3);
  or or_1 (out_4, and_1_out, and_2_out);
endmodule

module NOR (
  input  EN,
  input  [7:0] in_2,
  input  [7:0] in_3,
  output [7:0] out_4
);

  wire not_1_out;

  not not_1 (not_1_out, EN);
  nor nor_1 (out_4[0], in_2[0], not_1_out, in_3[0]);
  nor nor_2 (out_4[1], in_2[1], not_1_out, in_3[1]);
  nor nor_3 (out_4[2], in_2[2], not_1_out, in_3[2]);
  nor nor_4 (out_4[3], in_2[3], not_1_out, in_3[3]);
  nor nor_5 (out_4[4], in_2[4], not_1_out, in_3[4]);
  nor nor_6 (out_4[5], in_2[5], not_1_out, in_3[5]);
  nor nor_7 (out_4[6], in_2[6], not_1_out, in_3[6]);
  nor nor_8 (out_4[7], in_2[7], not_1_out, in_3[7]);
endmodule

module NAND (
  input  EN,
  input  [7:0] in_2,
  input  [7:0] in_3,
  output [7:0] out_4
);

  nand nand_1 (out_4[0], in_2[0], EN, in_3[0]);
  nand nand_2 (out_4[1], in_2[1], EN, in_3[1]);
  nand nand_3 (out_4[2], in_2[2], EN, in_3[2]);
  nand nand_4 (out_4[3], in_2[3], EN, in_3[3]);
  nand nand_5 (out_4[4], in_2[4], EN, in_3[4]);
  nand nand_6 (out_4[5], in_2[5], EN, in_3[5]);
  nand nand_7 (out_4[6], in_2[6], EN, in_3[6]);
  nand nand_8 (out_4[7], in_2[7], EN, in_3[7]);
endmodule

module XNOR (
  input  EN,
  input  [7:0] in_2,
  input  [7:0] in_3,
  output [7:0] out_4
);

  xnor_unit xnor_unit_1 (.EN(EN), .in_2(in_2[0]), .in_3(in_3[0]), .out_4(out_4[0]));
  xnor_unit xnor_unit_2 (.EN(EN), .in_2(in_2[1]), .in_3(in_3[1]), .out_4(out_4[1]));
  xnor_unit xnor_unit_3 (.EN(EN), .in_2(in_2[2]), .in_3(in_3[2]), .out_4(out_4[2]));
  xnor_unit xnor_unit_4 (.EN(EN), .in_2(in_2[3]), .in_3(in_3[3]), .out_4(out_4[3]));
  xnor_unit xnor_unit_5 (.EN(EN), .in_2(in_2[4]), .in_3(in_3[4]), .out_4(out_4[4]));
  xnor_unit xnor_unit_6 (.EN(EN), .in_2(in_2[5]), .in_3(in_3[5]), .out_4(out_4[5]));
  xnor_unit xnor_unit_7 (.EN(EN), .in_2(in_2[6]), .in_3(in_3[6]), .out_4(out_4[6]));
  xnor_unit xnor_unit_8 (.EN(EN), .in_2(in_2[7]), .in_3(in_3[7]), .out_4(out_4[7]));
endmodule

// XOR
module \xor  (
  input  EN,
  input  [7:0] in_2,
  input  [7:0] in_3,
  output [7:0] out_4
);

  XOR_unit xor_unit_1 (.en(EN), .in_2(in_2[0]), .in_3(in_3[0]), .out_4(out_4[0]));
  XOR_unit xor_unit_2 (.en(EN), .in_2(in_2[1]), .in_3(in_3[1]), .out_4(out_4[1]));
  XOR_unit xor_unit_3 (.en(EN), .in_2(in_2[2]), .in_3(in_3[2]), .out_4(out_4[2]));
  XOR_unit xor_unit_4 (.en(EN), .in_2(in_2[3]), .in_3(in_3[3]), .out_4(out_4[3]));
  XOR_unit xor_unit_5 (.en(EN), .in_2(in_2[4]), .in_3(in_3[4]), .out_4(out_4[4]));
  XOR_unit xor_unit_6 (.en(EN), .in_2(in_2[5]), .in_3(in_3[5]), .out_4(out_4[5]));
  XOR_unit xor_unit_7 (.en(EN), .in_2(in_2[6]), .in_3(in_3[6]), .out_4(out_4[6]));
  XOR_unit xor_unit_8 (.en(EN), .in_2(in_2[7]), .in_3(in_3[7]), .out_4(out_4[7]));
endmodule

// 2S COM
module _2ND_COMPLEMENT (
  input  [7:0] DI,
  input  EN,
  output [7:0] out_3
);

  wire [7:0] xnor_1_out;

  xnor xnor_1 (xnor_1_out[0], 1'b0, DI[0]);
  xnor xnor_2 (xnor_1_out[1], 1'b0, DI[1]);
  xnor xnor_3 (xnor_1_out[2], 1'b0, DI[2]);
  xnor xnor_4 (xnor_1_out[3], 1'b0, DI[3]);
  xnor xnor_5 (xnor_1_out[4], 1'b0, DI[4]);
  xnor xnor_6 (xnor_1_out[5], 1'b0, DI[5]);
  xnor xnor_7 (xnor_1_out[6], 1'b0, DI[6]);
  xnor xnor_8 (xnor_1_out[7], 1'b0, DI[7]);
  FULL_ADDER full_adder_1 (.D_I1(xnor_1_out), .D_I2(8'h1), .EN(EN), .Sout(out_3));  // open: Co
endmodule

// ADD
module FULL_ADDER (
  input  [7:0] D_I1,
  input  [7:0] D_I2,
  input  EN,
  output [7:0] Sout,
  output Co
);

  wire addder_unit_1_out_6, addder_unit_2_out_6, addder_unit_3_out_6, addder_unit_4_out_6,
       addder_unit_5_out_6, addder_unit_6_out_6, addder_unit_7_out_6;

  ADDDER_UNIT addder_unit_1 (
    .in_1(EN), .in_2(D_I1[0]), .in_3(D_I2[0]), .in_4(1'b0), .out_5(Sout[0]), .out_6(addder_unit_1_out_6));
  ADDDER_UNIT addder_unit_2 (
    .in_1(EN), .in_2(D_I1[1]), .in_3(D_I2[1]), .in_4(addder_unit_1_out_6), .out_5(Sout[1]),
    .out_6(addder_unit_2_out_6));
  ADDDER_UNIT addder_unit_3 (
    .in_1(EN), .in_2(D_I1[2]), .in_3(D_I2[2]), .in_4(addder_unit_2_out_6), .out_5(Sout[2]),
    .out_6(addder_unit_3_out_6));
  ADDDER_UNIT addder_unit_4 (
    .in_1(EN), .in_2(D_I1[3]), .in_3(D_I2[3]), .in_4(addder_unit_3_out_6), .out_5(Sout[3]),
    .out_6(addder_unit_4_out_6));
  ADDDER_UNIT addder_unit_5 (
    .in_1(EN), .in_2(D_I1[4]), .in_3(D_I2[4]), .in_4(addder_unit_4_out_6), .out_5(Sout[4]),
    .out_6(addder_unit_5_out_6));
  ADDDER_UNIT addder_unit_6 (
    .in_1(EN), .in_2(D_I1[5]), .in_3(D_I2[5]), .in_4(addder_unit_5_out_6), .out_5(Sout[5]),
    .out_6(addder_unit_6_out_6));
  ADDDER_UNIT addder_unit_7 (
    .in_1(EN), .in_2(D_I1[6]), .in_3(D_I2[6]), .in_4(addder_unit_6_out_6), .out_5(Sout[6]),
    .out_6(addder_unit_7_out_6));
  ADDDER_UNIT addder_unit_8 (
    .in_1(EN), .in_2(D_I1[7]), .in_3(D_I2[7]), .in_4(addder_unit_7_out_6), .out_5(Sout[7]), .out_6(Co));
endmodule

module xnor_unit (
  input  EN,
  input  in_2,
  input  in_3,
  output out_4
);

  wire and_1_out, and_2_out, not_1_out, not_2_out;

  and and_1 (and_1_out, in_2, EN, in_3);
  not not_1 (not_1_out, in_2);
  not not_2 (not_2_out, in_3);
  and and_2 (and_2_out, not_1_out, EN, not_2_out);
  or or_1 (out_4, and_1_out, and_2_out);
endmodule

module IR (
  input  [7:0] DI,
  input  load,
  input  CLK,
  input  RESET,
  input  OE,
  output [7:0] CONTENT,
  output [7:0] DO
);

  wire and_1_out, and_2_out, and_3_out, and_4_out, and_5_out, and_6_out, and_7_out, and_8_out, and_9_out,
       and_10_out, and_11_out, and_12_out, and_13_out, and_14_out, and_15_out, and_16_out, not_1_out,
       or_1_out, or_2_out, or_3_out, or_4_out, or_5_out, or_6_out, or_7_out, or_8_out;

  not not_1 (not_1_out, load);
  and and_1 (and_1_out, DI[7], load);
  or or_1 (or_1_out, and_1_out, and_2_out);
  and and_2 (and_2_out, not_1_out, CONTENT[7]);
  and and_3 (and_3_out, DI[6], load);
  D_Flip_Flop d_ff_1 (.clk(CLK), .D(or_1_out), .Q(CONTENT[7]), .reset(RESET));  // open: Qn, preset, en
  and and_4 (and_4_out, not_1_out, CONTENT[6]);
  or or_2 (or_2_out, and_3_out, and_4_out);
  and and_5 (and_5_out, DI[5], load);
  or or_3 (or_3_out, and_5_out, and_6_out);
  D_Flip_Flop d_ff_2 (.clk(CLK), .D(or_2_out), .Q(CONTENT[6]), .reset(RESET));  // open: Qn, preset, en
  and and_6 (and_6_out, not_1_out, CONTENT[5]);
  D_Flip_Flop d_ff_3 (.clk(CLK), .D(or_3_out), .Q(CONTENT[5]), .reset(RESET));  // open: Qn, preset, en
  and and_7 (and_7_out, DI[4], load);
  or or_4 (or_4_out, and_7_out, and_8_out);
  and and_8 (and_8_out, not_1_out, CONTENT[4]);
  D_Flip_Flop d_ff_4 (.clk(CLK), .D(or_4_out), .Q(CONTENT[4]), .reset(RESET));  // open: Qn, preset, en
  and and_9 (and_9_out, DI[3], load);
  and and_10 (and_10_out, not_1_out, CONTENT[3]);
  or or_5 (or_5_out, and_9_out, and_10_out);
  D_Flip_Flop d_ff_5 (.clk(CLK), .D(or_5_out), .Q(CONTENT[3]), .reset(RESET));  // open: Qn, preset, en
  and and_11 (and_11_out, DI[2], load);
  or or_6 (or_6_out, and_11_out, and_12_out);
  and and_12 (and_12_out, not_1_out, CONTENT[2]);
  and and_13 (and_13_out, DI[1], load);
  D_Flip_Flop d_ff_6 (.clk(CLK), .D(or_6_out), .Q(CONTENT[2]), .reset(RESET));  // open: Qn, preset, en
  and and_14 (and_14_out, not_1_out, CONTENT[1]);
  or or_7 (or_7_out, and_13_out, and_14_out);
  D_Flip_Flop d_ff_7 (.clk(CLK), .D(or_7_out), .Q(CONTENT[1]), .reset(RESET));  // open: Qn, preset, en
  and and_15 (and_15_out, DI[0], load);
  or or_8 (or_8_out, and_15_out, and_16_out);
  and and_16 (and_16_out, not_1_out, CONTENT[0]);
  D_Flip_Flop d_ff_8 (.clk(CLK), .D(or_8_out), .Q(CONTENT[0]), .reset(RESET));  // open: Qn, preset, en
  assign DO = OE ? CONTENT : 8'bz;  // Controlled_Buffer controlled_buffer_1
endmodule

// CU
module CU_2 (
  input  OPC3,
  input  OPC2,
  input  OPC1,
  input  OPC0,
  input  SC2,
  input  SC1,
  input  SC0,
  output C12,
  output C13,
  output C14,
  output C15,
  output C16,
  output C17
);

  wire and_1_out, and_2_out, and_3_out, and_4_out, and_5_out, and_6_out, and_7_out, and_8_out, and_9_out,
       and_10_out, and_11_out, and_12_out, and_13_out, and_14_out, and_15_out, and_16_out, and_17_out,
       and_18_out, not_1_out, not_2_out, not_3_out, not_4_out, not_5_out, not_6_out, not_7_out, not_8_out,
       not_9_out, not_10_out, not_11_out, not_12_out, not_13_out, not_14_out, not_15_out, not_16_out,
       not_17_out, not_18_out, not_19_out, not_20_out, not_21_out, not_22_out, not_23_out, not_24_out,
       not_25_out, not_26_out, not_27_out, not_28_out, not_29_out, not_30_out, not_31_out, not_32_out,
       not_33_out, not_34_out, not_35_out, not_36_out, not_37_out, not_38_out, not_39_out, not_40_out,
       not_41_out, not_42_out, not_43_out, not_44_out, not_45_out, not_46_out, not_47_out, not_48_out,
       not_49_out, not_50_out, not_51_out, not_52_out, not_53_out, not_54_out, not_55_out, not_56_out,
       not_57_out;

  not not_1 (not_1_out, OPC3);
  not not_2 (not_2_out, OPC2);
  not not_3 (not_3_out, OPC1);
  not not_4 (not_4_out, SC1);
  not not_5 (not_5_out, OPC1);
  not not_6 (not_6_out, OPC0);
  not not_7 (not_7_out, SC1);
  not not_8 (not_8_out, OPC3);
  not not_9 (not_9_out, OPC2);
  not not_10 (not_10_out, OPC0);
  not not_11 (not_11_out, SC1);
  not not_12 (not_12_out, OPC1);
  not not_13 (not_13_out, SC1);
  not not_14 (not_14_out, OPC1);
  not not_15 (not_15_out, SC1);
  not not_16 (not_16_out, OPC3);
  not not_17 (not_17_out, OPC1);
  not not_18 (not_18_out, OPC0);
  not not_19 (not_19_out, SC2);
  not not_20 (not_20_out, SC2);
  not not_21 (not_21_out, SC2);
  not not_22 (not_22_out, OPC2);
  not not_23 (not_23_out, OPC0);
  not not_24 (not_24_out, SC2);
  not not_25 (not_25_out, OPC3);
  not not_26 (not_26_out, OPC2);
  not not_27 (not_27_out, SC2);
  not not_28 (not_28_out, OPC0);
  not not_29 (not_29_out, SC2);
  not not_30 (not_30_out, OPC0);
  not not_31 (not_31_out, SC2);
  not not_32 (not_32_out, OPC3);
  not not_33 (not_33_out, OPC2);
  not not_34 (not_34_out, SC1);
  not not_35 (not_35_out, SC0);
  not not_36 (not_36_out, OPC3);
  not not_37 (not_37_out, OPC1);
  not not_38 (not_38_out, OPC0);
  not not_39 (not_39_out, SC1);
  not not_40 (not_40_out, OPC3);
  not not_41 (not_41_out, OPC2);
  not not_42 (not_42_out, OPC1);
  not not_43 (not_43_out, SC1);
  not not_44 (not_44_out, OPC3);
  not not_45 (not_45_out, OPC2);
  not not_46 (not_46_out, OPC0);
  not not_47 (not_47_out, SC1);
  not not_48 (not_48_out, OPC3);
  not not_49 (not_49_out, OPC2);
  not not_50 (not_50_out, SC2);
  not not_51 (not_51_out, SC0);
  not not_52 (not_52_out, OPC3);
  not not_53 (not_53_out, OPC1);
  not not_54 (not_54_out, OPC0);
  not not_55 (not_55_out, SC2);
  not not_56 (not_56_out, SC1);
  not not_57 (not_57_out, SC0);
  and and_1 (and_1_out, not_1_out, not_2_out, not_3_out, SC2, not_4_out, SC0);
  and and_2 (and_2_out, not_5_out, not_6_out, SC2, not_7_out, SC0);
  and and_3 (and_3_out, not_8_out, not_9_out, OPC1, not_10_out, SC2, not_11_out, SC0);
  and and_4 (and_4_out, OPC2, not_12_out, OPC0, SC2, not_13_out, SC0);
  and and_5 (and_5_out, OPC3, not_14_out, OPC0, SC2, not_15_out, SC0);
  and and_6 (and_6_out, not_16_out, OPC2, not_17_out, not_18_out, not_19_out, SC1, SC0);
  and and_7 (and_7_out, OPC2, OPC1, OPC0, not_20_out, SC1, SC0);
  and and_8 (and_8_out, OPC3, OPC1, OPC0, not_21_out, SC1, SC0);
  and and_9 (and_9_out, not_22_out, not_23_out, not_24_out, SC1, SC0);
  and and_10 (and_10_out, not_25_out, not_26_out, OPC1, not_27_out, SC1, SC0);
  and and_11 (and_11_out, OPC1, not_28_out, not_29_out, SC1, SC0);
  and and_12 (and_12_out, OPC3, not_30_out, not_31_out, SC1, SC0);
  and and_13 (and_13_out, not_32_out, not_33_out, OPC1, OPC0, SC2, not_34_out, not_35_out);
  and and_14 (and_14_out, not_36_out, OPC2, not_37_out, not_38_out, SC2, not_39_out, SC0);
  and and_15 (and_15_out, not_40_out, not_41_out, not_42_out, OPC0, SC2, not_43_out, SC0);
  and and_16 (and_16_out, not_44_out, not_45_out, OPC1, not_46_out, SC2, not_47_out, SC0);
  and and_17 (and_17_out, not_48_out, not_49_out, OPC1, OPC0, not_50_out, SC1, not_51_out);
  and and_18 (and_18_out, not_52_out, OPC2, not_53_out, not_54_out, not_55_out, not_56_out, not_57_out);
  or or_1 (C12, and_1_out, and_2_out);
  or or_2 (C13, and_3_out, and_4_out, and_5_out);
  or or_3 (C14, and_6_out, and_7_out, and_8_out);
  or or_4 (C15, and_9_out, and_10_out, and_11_out, and_12_out);
  or or_5 (C16, and_13_out, and_14_out);
  or or_6 (C17, and_15_out, and_16_out, and_17_out, and_18_out);
endmodule

module CU (
  input  OPC3,
  input  OPC2,
  input  OPC1,
  input  OPC0,
  input  SC2,
  input  SC1,
  input  SC0,
  output C0,
  output C1,
  output C2,
  output C3,
  output C4,
  output C5,
  output C6,
  output C7,
  output C8,
  output C9,
  output C10,
  output C11
);

  wire and_4_out, and_5_out, and_6_out, and_7_out, and_8_out, and_9_out, and_10_out, and_13_out, and_14_out,
       and_15_out, and_16_out, and_17_out, and_18_out, and_19_out, and_20_out, not_1_out, not_2_out,
       not_3_out, not_4_out, not_5_out, not_6_out, not_7_out, not_8_out, not_9_out, not_10_out, not_11_out,
       not_12_out, not_13_out, not_14_out, not_15_out, not_16_out, not_17_out, not_18_out, not_19_out,
       not_20_out, not_21_out, not_22_out, not_23_out, not_24_out, not_25_out, not_26_out, not_27_out,
       not_28_out, not_29_out, not_30_out, not_31_out, not_32_out, not_33_out, not_34_out, not_35_out,
       not_36_out, not_37_out, not_38_out, not_39_out, not_40_out, not_41_out, not_42_out, not_43_out,
       not_44_out;

  not not_1 (not_1_out, SC2);
  not not_2 (not_2_out, SC1);
  not not_3 (not_3_out, SC0);
  not not_4 (not_4_out, SC2);
  not not_5 (not_5_out, SC1);
  not not_6 (not_6_out, SC1);
  not not_7 (not_7_out, SC0);
  not not_8 (not_8_out, SC2);
  not not_9 (not_9_out, SC1);
  not not_10 (not_10_out, OPC1);
  not not_11 (not_11_out, SC1);
  not not_12 (not_12_out, SC0);
  not not_13 (not_13_out, SC2);
  not not_14 (not_14_out, SC1);
  not not_15 (not_15_out, OPC1);
  not not_16 (not_16_out, SC1);
  not not_17 (not_17_out, SC0);
  not not_18 (not_18_out, SC2);
  not not_19 (not_19_out, SC2);
  not not_20 (not_20_out, SC0);
  not not_21 (not_21_out, OPC1);
  not not_22 (not_22_out, SC1);
  not not_23 (not_23_out, SC1);
  not not_24 (not_24_out, SC0);
  not not_25 (not_25_out, SC2);
  not not_26 (not_26_out, SC0);
  not not_27 (not_27_out, OPC1);
  not not_28 (not_28_out, SC2);
  not not_29 (not_29_out, SC2);
  not not_30 (not_30_out, SC2);
  not not_31 (not_31_out, SC1);
  not not_32 (not_32_out, SC0);
  not not_33 (not_33_out, OPC1);
  not not_34 (not_34_out, SC2);
  not not_35 (not_35_out, SC2);
  not not_36 (not_36_out, SC2);
  not not_37 (not_37_out, SC1);
  not not_38 (not_38_out, OPC1);
  not not_39 (not_39_out, SC1);
  not not_40 (not_40_out, SC0);
  not not_41 (not_41_out, SC1);
  not not_42 (not_42_out, SC0);
  not not_43 (not_43_out, OPC0);
  not not_44 (not_44_out, SC2);
  and and_1 (C0, not_1_out, not_2_out, not_3_out);
  and and_2 (C1, not_4_out, not_5_out, SC0);
  and and_3 (C2, OPC1, OPC0, SC2, not_6_out, not_7_out);
  and and_4 (and_4_out, not_8_out, not_9_out, SC0);
  and and_5 (and_5_out, not_10_out, SC2, not_11_out, not_12_out);
  and and_6 (and_6_out, not_13_out, not_14_out, SC0);
  and and_7 (and_7_out, not_15_out, SC2, not_16_out, not_17_out);
  and and_8 (and_8_out, OPC1, OPC0, not_18_out, SC0);
  and and_9 (and_9_out, not_19_out, SC1, not_20_out);
  and and_10 (and_10_out, not_21_out, SC2, not_22_out, SC0);
  and and_11 (C6, OPC1, OPC0, SC2, not_23_out, not_24_out);
  and and_12 (C7, not_25_out, SC1, not_26_out);
  and and_13 (and_13_out, not_27_out, not_28_out, SC1, SC0);
  and and_14 (and_14_out, OPC0, not_29_out, SC1, SC0);
  and and_15 (and_15_out, not_30_out, not_31_out, not_32_out);
  and and_16 (and_16_out, not_33_out, not_34_out, SC1, SC0);
  and and_17 (and_17_out, OPC0, not_35_out, SC1, SC0);
  and and_18 (and_18_out, not_36_out, not_37_out, SC0);
  and and_19 (and_19_out, not_38_out, SC2, not_39_out, not_40_out);
  and and_20 (and_20_out, OPC0, SC2, not_41_out, not_42_out);
  and and_21 (C11, OPC1, not_43_out, not_44_out, SC1, SC0);
  or or_1 (C3, and_4_out, and_5_out);
  or or_2 (C4, and_6_out, and_7_out, and_8_out);
  or or_3 (C5, and_9_out, and_10_out);
  or or_4 (C8, and_13_out, and_14_out);
  or or_5 (C9, and_15_out, and_16_out, and_17_out);
  or or_6 (C10, and_18_out, and_19_out, and_20_out);
endmodule
